# Fritzing sketch lichtschranke (saved by Fritzing 0.9.10b)

parts:
  U1 = ESP32-38PinWide [part_number=ESP32-38PinWide]
  LD1 = LD  # not connected
  R1 = Photocell (LDR) [package=THT]
  R4 = Resistor [tolerance=±5% power=0.25 resistance=220 package=THT]
  S6 = Pushbutton [package="[THT]"]
  R5 = Resistor [tolerance=±5% power=0.25 resistance=100k package=THT]  # not connected

nets:
  N1: U1.GPIO34, R1.pin_1
  N2: U1.GPIO33, U1.VIN, R1.pin_0, S6.Pin_3, S6.Pin_4
  N3: U1.GND, R4.Pin_0

notes:
  5V
  GND
  100KΩ
  220 Ω

custom parts:
  ESP32-38PinWide: Generic 38-Pin ESP32 with wide format (only access to one side of pins on a breadboard) based on Stephen Lilley's HiLetgo ESP-WROOM-32 ESP32 ESP-32S Development Board.
  LD: A Generic Red Dot Laser Diode Module (~5mW)
